# Fritzing sketch LCD (saved by Fritzing 0.9.2b)
circuit board: 6.88566cm x 5.36311cm
breadboards: 2

parts:
  LCD1 = LCD screen
  R2 = Resistor [tolerance=±5% resistance=220 package=THT]
  Arduino1 = Arduino Uno (Rev3)
  R3 = Trimmer Potentiometer [maximum_resistance=10kΩ package=THT]  # not connected
  U1 = TEMPERATURE-SENSOR [package=to-92]  # not connected
  U2 = TEMPERATURE-SENSOR [package=to-92]  # not connected
  U3 = TEMPERATURE-SENSOR [package=to-92]  # not connected
  U4 = TEMPERATURE-SENSOR [package=to-92]  # not connected
  U5 = TEMPERATURE-SENSOR [package=to-92]  # not connected
  U6 = TEMPERATURE-SENSOR [package=to-92]  # not connected
  U7 = HALL-EFFECT [package=sc70]  # not connected
  U8 = MAX6675 [package=so08]  # not connected

nets (from the pcb view):
  VSS: LCD1.VSS, LCD1.R/W, LCD1.LED-, Arduino1.GND
  N1: LCD1.RS, Arduino1.D12/MISO
  N2: LCD1.E, Arduino1.D11_PWM/MOSI
  N3: LCD1.DB4, Arduino1.D5_PWM
  N4: LCD1.DB5, Arduino1.D4
  N5: LCD1.DB6, Arduino1.D3_PWM
  N6: LCD1.DB7, Arduino1.D2
  N7: LCD1.LED+, R2.Pin_0
  N8: R2.Pin_1, Arduino1.5V

notes:
  Mesh of DS18B20 temp sensors
